// Logisim project ignition.circ as structural Verilog: 1 circuit, main circuit main
module main (
  input  start_engine,
  input  engine_running,
  output starter_motor,
  output ignition_coil
);

  wire and_1_out, and_2_out, and_3_out, and_4_out, and_5_out, and_6_out, and_7_out, and_8_out, and_10_out,
       clk, not_1_out, not_2_out, not_3_out, notQ0, notQ1, or_1_out, or_2_out, Q0, Q1;

  Clock clock_1 (.out(clk));
  not not_1 (not_1_out, engine_running);
  not not_2 (not_2_out, Q1);
  and and_1 (and_1_out, not_1_out, not_2_out, Q0);
  and and_2 (and_2_out, engine_running, Q1, Q0);
  and and_3 (and_3_out, not_2_out, start_engine);
  and and_4 (and_4_out, Q0, start_engine);
  and and_5 (and_5_out, engine_running, start_engine);
  not not_3 (not_3_out, start_engine);
  and and_6 (and_6_out, not_3_out, engine_running, Q0);
  and and_7 (and_7_out, start_engine, Q0, Q1);
  and and_8 (and_8_out, engine_running, Q1);
  or or_1 (or_1_out, and_1_out, and_2_out, and_3_out, and_4_out, and_5_out);
  or or_2 (or_2_out, and_6_out, and_7_out, and_8_out);
  D_Flip_Flop d_ff_1 (.D(or_2_out), .clk(clk), .Q(Q1), .Qn(notQ1));  // open: preset, reset
  D_Flip_Flop d_ff_2 (.D(or_1_out), .clk(clk), .Q(Q0), .Qn(notQ0));  // open: preset, reset
  and and_9 (starter_motor, notQ1, Q0);
  and and_10 (and_10_out, Q1, notQ0);
  or or_3 (ignition_coil, starter_motor, and_10_out);

  // Other names for the same wires on the sheet: ER = engine_running; SE = start_engine
endmodule
