// Logisim project my_adder.circ as structural Verilog: 2 circuits, main circuit main
module main (
  input  [15:0] A,
  input  [15:0] B,
  input  sub,
  output [15:0] result,
  output ovf
);

  wire full_adder_1_cout, full_adder_2_cout, full_adder_3_cout, full_adder_4_cout, full_adder_5_cout,
       full_adder_6_cout, full_adder_7_cout, full_adder_8_cout, full_adder_9_cout, full_adder_10_cout,
       full_adder_11_cout, full_adder_12_cout, full_adder_13_cout, full_adder_14_cout, full_adder_15_cout,
       full_adder_16_cout, xor_1_out, xor_2_out, xor_3_out, xor_4_out, xor_5_out, xor_6_out, xor_7_out,
       xor_8_out, xor_9_out, xor_10_out, xor_11_out, xor_12_out, xor_13_out, xor_14_out, xor_15_out,
       xor_16_out;

  xor xor_1 (xor_1_out, sub, B[0]);
  xor xor_2 (xor_2_out, sub, B[1]);
  xor xor_3 (xor_3_out, sub, B[2]);
  xor xor_4 (xor_4_out, sub, B[3]);
  xor xor_5 (xor_5_out, sub, B[4]);
  xor xor_6 (xor_6_out, sub, B[5]);
  xor xor_7 (xor_7_out, sub, B[6]);
  xor xor_8 (xor_8_out, sub, B[7]);
  full_adder full_adder_1 (.Cout(full_adder_1_cout), .sum(result[0]), .B(xor_1_out), .A(A[0]), .Cin(sub));
  full_adder full_adder_2 (.Cout(full_adder_2_cout), .sum(result[1]), .B(xor_2_out), .A(A[1]), .Cin(full_adder_1_cout));
  full_adder full_adder_3 (.Cout(full_adder_3_cout), .sum(result[2]), .B(xor_3_out), .A(A[2]), .Cin(full_adder_2_cout));
  full_adder full_adder_4 (.Cout(full_adder_4_cout), .sum(result[3]), .B(xor_4_out), .A(A[3]), .Cin(full_adder_3_cout));
  full_adder full_adder_5 (.Cout(full_adder_5_cout), .sum(result[4]), .B(xor_5_out), .A(A[4]), .Cin(full_adder_4_cout));
  full_adder full_adder_6 (.Cout(full_adder_6_cout), .sum(result[5]), .B(xor_6_out), .A(A[5]), .Cin(full_adder_5_cout));
  full_adder full_adder_7 (.Cout(full_adder_7_cout), .sum(result[6]), .B(xor_7_out), .A(A[6]), .Cin(full_adder_6_cout));
  full_adder full_adder_8 (.Cout(full_adder_8_cout), .sum(result[7]), .B(xor_8_out), .A(A[7]), .Cin(full_adder_7_cout));
  full_adder full_adder_9 (
    .Cout(full_adder_9_cout), .sum(result[15]), .B(xor_9_out), .A(A[15]), .Cin(full_adder_10_cout));
  full_adder full_adder_10 (
    .Cout(full_adder_10_cout), .sum(result[14]), .B(xor_10_out), .A(A[14]), .Cin(full_adder_11_cout));
  full_adder full_adder_11 (
    .Cout(full_adder_11_cout), .sum(result[13]), .B(xor_11_out), .A(A[13]), .Cin(full_adder_12_cout));
  full_adder full_adder_12 (
    .Cout(full_adder_12_cout), .sum(result[12]), .B(xor_12_out), .A(A[12]), .Cin(full_adder_13_cout));
  full_adder full_adder_13 (
    .Cout(full_adder_13_cout), .sum(result[11]), .B(xor_13_out), .A(A[11]), .Cin(full_adder_14_cout));
  full_adder full_adder_14 (
    .Cout(full_adder_14_cout), .sum(result[10]), .B(xor_14_out), .A(A[10]), .Cin(full_adder_15_cout));
  full_adder full_adder_15 (
    .Cout(full_adder_15_cout), .sum(result[9]), .B(xor_15_out), .A(A[9]), .Cin(full_adder_16_cout));
  full_adder full_adder_16 (
    .Cout(full_adder_16_cout), .sum(result[8]), .B(xor_16_out), .A(A[8]), .Cin(full_adder_8_cout));
  xor xor_9 (xor_9_out, B[15], sub);
  xor xor_10 (xor_10_out, B[14], sub);
  xor xor_11 (xor_11_out, B[13], sub);
  xor xor_12 (xor_12_out, B[12], sub);
  xor xor_13 (xor_13_out, B[11], sub);
  xor xor_14 (xor_14_out, B[10], sub);
  xor xor_15 (xor_15_out, B[9], sub);
  xor xor_16 (xor_16_out, B[8], sub);
  xor xor_17 (ovf, full_adder_9_cout, full_adder_10_cout);

  // Other names for the same wires on the sheet: A7[7:0] = A[7:0]; A16[7:0] = A[15:8]; B7[7:0] = B[7:0];
  //   B16[7:0] = B[15:8]
endmodule

module full_adder (
  input  Cin,
  input  A,
  input  B,
  output sum,
  output Cout
);

  wire and_1_out, and_2_out, xor_1_out;

  and and_1 (and_1_out, B, A);
  xor xor_1 (xor_1_out, A, B);
  or or_1 (Cout, and_1_out, and_2_out);
  and and_2 (and_2_out, xor_1_out, Cin);
  xor xor_2 (sum, Cin, xor_1_out);
endmodule
